// Logisim project CircuitoCifrado.circ as structural Verilog: 1 circuit, main circuit main
module main (
  input  [3:0] D,
  input  [3:0] Palabra_2,
  input  [3:0] Palabra_3,
  output [3:0] out_4,
  output [3:0] out_5,
  output [3:0] out_6
);

  wire and_1_out, and_2_out, and_3_out, and_4_out, and_5_out, and_6_out, and_7_out, and_8_out, and_9_out,
       and_10_out, not_2_out, not_3_out, not_4_out, not_6_out;

  not not_1 (out_6[0], Palabra_3[0]);
  not not_2 (not_2_out, Palabra_3[1]);
  not not_3 (not_3_out, Palabra_3[2]);
  not not_4 (not_4_out, Palabra_3[3]);
  not not_5 (out_4[2], D[2]);
  not not_6 (not_6_out, D[3]);
  not not_7 (out_5[3], Palabra_2[3]);
  and and_1 (and_1_out, Palabra_3[3], not_2_out, out_6[0]);
  and and_2 (and_2_out, not_4_out, Palabra_3[2], Palabra_3[1]);
  and and_3 (and_3_out, not_4_out, Palabra_3[2], Palabra_3[0]);
  and and_4 (and_4_out, D[3], out_4[2]);
  and and_5 (and_5_out, not_6_out, D[2]);
  and and_6 (and_6_out, Palabra_3[0], Palabra_3[1]);
  and and_7 (and_7_out, out_6[0], not_3_out, Palabra_3[1]);
  and and_8 (and_8_out, Palabra_3[0], not_3_out);
  and and_9 (and_9_out, out_6[0], Palabra_3[2], not_2_out);
  or or_1 (out_6[3], Palabra_3[3], and_1_out, and_2_out, and_3_out);
  or or_2 (out_4[3], and_4_out, and_5_out);
  or or_3 (out_6[1], and_6_out, and_10_out);
  and and_10 (and_10_out, out_6[0], not_2_out);
  or or_4 (out_6[2], and_7_out, and_8_out, and_9_out);

  assign out_4[1:0] = D[1:0];
  assign out_5[2:0] = Palabra_2[2:0];

  // Notes on the sheet:
  //   Cifrado
  //   A
  //   B
  //   C
  //   Palabra 1
  //   c
  //   b
  //   d
  //   a
endmodule
