// Logisim project CircuitoDescifrado.circ as structural Verilog: 1 circuit, main circuit main
module main (
  input  [3:0] Palabra_1,
  input  [3:0] in_2,
  input  [3:0] Palabra_2,
  output [3:0] out_4,
  output [3:0] out_5,
  output [3:0] out_6
);

  wire and_1_out, and_2_out, and_3_out, and_4_out, and_5_out, and_6_out, and_7_out, and_8_out, and_9_out,
       and_10_out, and_11_out, not_1_out, not_2_out, not_5_out, not_6_out, not_7_out, not_8_out, not_9_out,
       not_10_out, not_11_out, not_12_out, not_13_out, not_14_out, not_15_out, not_16_out;

  not not_1 (not_1_out, Palabra_1[3]);
  not not_2 (not_2_out, Palabra_1[2]);
  not not_3 (out_4[2], Palabra_1[2]);
  not not_4 (out_6[3], Palabra_2[3]);
  and and_1 (and_1_out, not_1_out, not_2_out);
  and and_2 (and_2_out, Palabra_1[3], Palabra_1[2]);
  or or_1 (out_4[3], and_1_out, and_2_out);
  not not_5 (not_5_out, in_2[3]);
  not not_6 (not_6_out, in_2[2]);
  not not_7 (not_7_out, in_2[1]);
  not not_8 (not_8_out, in_2[3]);
  not not_9 (not_9_out, in_2[2]);
  not not_10 (not_10_out, in_2[0]);
  not not_11 (not_11_out, in_2[2]);
  not not_12 (not_12_out, in_2[1]);
  not not_13 (not_13_out, in_2[2]);
  not not_14 (not_14_out, in_2[0]);
  not not_15 (not_15_out, in_2[1]);
  not not_16 (not_16_out, in_2[0]);
  not not_17 (out_5[0], in_2[0]);
  and and_3 (and_3_out, not_5_out, not_6_out, not_7_out);
  and and_4 (and_4_out, not_8_out, not_9_out, not_10_out);
  and and_5 (and_5_out, in_2[3], in_2[1], in_2[0]);
  and and_6 (and_6_out, in_2[3], in_2[2]);
  and and_7 (and_7_out, not_11_out, not_12_out);
  and and_8 (and_8_out, not_13_out, not_14_out);
  and and_9 (and_9_out, in_2[2], in_2[1], in_2[0]);
  and and_10 (and_10_out, not_15_out, in_2[0]);
  and and_11 (and_11_out, in_2[1], not_16_out);
  or or_2 (out_5[3], and_3_out, and_4_out, and_5_out, and_6_out);
  or or_3 (out_5[2], and_7_out, and_8_out, and_9_out);
  or or_4 (out_5[1], and_10_out, and_11_out);

  assign out_4[1:0] = Palabra_1[1:0];
  assign out_6[2:0] = Palabra_2[2:0];

  // Notes on the sheet:
  //   Descifrado
  //   Palabra 3
endmodule
