// Logisim project Circuito1.circ as structural Verilog: 2 circuits, main circuit Circuito 1
module Circuito_1 (
  input  Reset,
  output [2:0] Contador
);

  wire cambioestados_1_q3, cambioestados_1_q4, cambioestados_1_q5, clock_1_out;

  cambioEstados cambioestados_1 (
    .r(Reset), .q0(Contador[2]), .q1(Contador[1]), .q2(Contador[0]), .q3(cambioestados_1_q3),
    .q4(cambioestados_1_q4), .q5(cambioestados_1_q5));
  Clock clock_1 (.out(clock_1_out));
  D_Flip_Flop d_ff_1 (.clk(clock_1_out), .D(cambioestados_1_q3), .Q(Contador[2]));  // open: Qn, preset, en, reset
  D_Flip_Flop d_ff_2 (.clk(clock_1_out), .D(cambioestados_1_q4), .Q(Contador[1]));  // open: Qn, preset, en, reset
  D_Flip_Flop d_ff_3 (.clk(clock_1_out), .D(cambioestados_1_q5), .Q(Contador[0]));  // open: Qn, preset, en, reset
endmodule

module cambioEstados (
  input  r,
  input  q0,
  input  q1,
  input  q2,
  output q3,
  output q4,
  output q5
);

  wire and_1_out, and_2_out, and_4_out, and_5_out, and_6_out, not_1_out, not_2_out, not_3_out, not_4_out,
       not_5_out, not_6_out, not_7_out, not_8_out, not_9_out, not_10_out, not_11_out, not_12_out;

  not not_1 (not_1_out, r);
  not not_2 (not_2_out, q0);
  not not_3 (not_3_out, r);
  not not_4 (not_4_out, q1);
  not not_5 (not_5_out, r);
  not not_6 (not_6_out, q2);
  not not_7 (not_7_out, r);
  not not_8 (not_8_out, q1);
  and and_1 (and_1_out, not_7_out, not_8_out, q2);
  not not_9 (not_9_out, r);
  and and_2 (and_2_out, not_9_out, q1, not_10_out);
  not not_10 (not_10_out, q2);
  not not_11 (not_11_out, r);
  and and_3 (q5, not_11_out, not_12_out);
  not not_12 (not_12_out, q2);
  and and_4 (and_4_out, not_1_out, not_2_out, q1, q2);
  and and_5 (and_5_out, not_3_out, q0, not_4_out);
  or or_1 (q3, and_4_out, and_5_out, and_6_out);
  and and_6 (and_6_out, not_5_out, q0, not_6_out);
  or or_2 (q4, and_1_out, and_2_out);
endmodule
