// Logisim project Circuito2.circ as structural Verilog: 1 circuit, main circuit main
module main (
  input  E,
  output Y
);

  wire and_1_out, and_2_out, and_3_out, and_4_out, clock_1_out, not_1_out, or_1_out, Q1_qn, Q2_q, Q2_qn,
       Q3_q, Q3_qn;

  not not_1 (not_1_out, E);
  and and_1 (and_1_out, not_1_out, Q3_q, Q2_qn);
  and and_2 (and_2_out, E, Q2_q, Q3_qn);
  and and_3 (and_3_out, E, Y, Q3_qn);
  Clock clock_1 (.out(clock_1_out));
  and and_4 (and_4_out, Q2_q, Q3_q);
  or or_1 (or_1_out, and_1_out, and_2_out, and_3_out);
  D_Flip_Flop Q1 (.clk(clock_1_out), .D(and_4_out), .Q(Y), .Qn(Q1_qn));  // open: preset, en, reset
  D_Flip_Flop Q2 (.clk(clock_1_out), .D(or_1_out), .Q(Q2_q), .Qn(Q2_qn));  // open: preset, en, reset
  D_Flip_Flop Q3 (.clk(clock_1_out), .D(E), .Q(Q3_q), .Qn(Q3_qn));  // open: preset, en, reset
endmodule
